# Fritzing sketch Circuit Diagram (saved by Fritzing 0.8.7b)
breadboards: 2

parts:
  Part3 = Arduino Nano (Rev3.0)
  M2 = DC Motor
  M3 = DC Motor
  Part4 = SRF05 Ultrasonic Rangefinder
  U1 = L9110 H-bridge module [part_number="L9110 H-bridge"]
  M4 = fc-51 [package=THT]
  M5 = fc-51 [package=THT]
  U2 = LIPO-1000mAh [package=lipo-1000]
  S1 = Toggle Switch spst [package=THT]
  C1 = Ceramic Capacitor [capacitance="100 nF" package="0603 [SMD, multilayer]"]
  VCC1 = 4 x AAA Battery Mount

nets:
  GND: Part3.GND, Part4.GND, U1.GND, M4.pin2, M5.pin2, U2.-, C1.0, VCC1.-
  N1: Part3.D3, Part4.Trig
  N2: Part3.D4, Part4.Echo
  N3: Part3.D5, U1.B-IA
  N4: Part3.D6, U1.B-IB
  N5: Part3.D7, M5.pin1
  N6: Part3.D8, M4.pin1
  N7: Part3.D10, U1.A-IA
  N8: Part3.D11/MOSI, U1.A-IB
  N9: Part3.VIN, S1.COM
  VCC: Part3.5V, Part4.VCC, U1.VCC, U2.+, C1.1
  N10: Part3.3V3, M4.pin3, M5.pin3
  N11: M2.pin_1, U1.MOTOR_B-B
  N12: M2.pin_2, U1.MOTOR_B-A
  N13: M3.pin_1, U1.MOTOR_A-B
  N14: M3.pin_2, U1.MOTOR_A-A
  N15: S1.L1, VCC1.+

custom parts:
  Toggle Switch spst: Toggle Switch single pole single throw
